// Digital circuit subtractor.dig as structural Verilog
module subtractor (
  input  in_1,
  input  in_2,
  input  in_3,
  input  in_4,
  input  in_5,
  input  in_6,
  input  in_7,
  input  in_8,
  output R0,
  output R1,
  output R2,
  output R3,
  output R4
);

  wire sub_1_c_o, sub_2_c_o, sub_3_c_o;

  Sub sub_1 (.a(in_1), .b(in_5), .c_i(1'b0), .s(R0), .c_o(sub_1_c_o));
  Sub sub_2 (.a(in_2), .b(in_6), .c_i(sub_1_c_o), .s(R1), .c_o(sub_2_c_o));
  Sub sub_3 (.a(in_3), .b(in_7), .c_i(sub_2_c_o), .s(R2), .c_o(sub_3_c_o));
  Sub sub_4 (.a(in_4), .b(in_8), .c_i(sub_3_c_o), .s(R3), .c_o(R4));
endmodule
